# Fritzing sketch 2x6_Button_matrix (saved by Fritzing 0.9.3b)
breadboards: 2

parts:
  U1 = DIODE-ZENER [package=diode-zener]
  U2 = DIODE-ZENER [package=diode-zener]
  U3 = DIODE-ZENER [package=diode-zener]
  U4 = DIODE-ZENER [package=diode-zener]
  U5 = DIODE-ZENER [package=diode-zener]
  U6 = DIODE-ZENER [package=diode-zener]
  S1 = Momentary Switch [package=ksa_sealed_tac_switch]
  S2 = Momentary Switch [package=ksa_sealed_tac_switch]
  S3 = Momentary Switch [package=ksa_sealed_tac_switch]
  S4 = Momentary Switch [package=ksa_sealed_tac_switch]
  S5 = Momentary Switch [package=ksa_sealed_tac_switch]
  S6 = Momentary Switch [package=ksa_sealed_tac_switch]
  Part1 = Arduino Uno (Rev3)

nets:
  N1: U1.C, Part1.D3_PWM
  N2: U1.A, U6.C, S3.4
  N3: U2.C, U6.A, S2.4
  N4: U2.A, S1.4
  N5: U3.C, U5.A, S4.4
  N6: U3.A, U4.C, S6.4
  N7: U4.A, S5.4
  N8: U5.C, Part1.D2
  N9: S1.1, Part1.D4
  N10: S1.2, S5.1
  N11: S2.1, Part1.D5_PWM
  N12: S2.2, S6.1
  N13: S3.1, Part1.D6_PWM
  N14: S3.2, S4.1
